# Fritzing sketch Digital_Clock (saved by Fritzing 1.0.5)
breadboards: 1

parts:
  µC1 = ATmega32 [package=dip]
  Matrix_keypad1 = KEYPAD 4x4
  U1 = LCD-16X2 [package=lcd-16x2_noholes]
  U2 = POT_SWITCH [knob_status=50% power=0.5W package=pot_pth]
  J1 = Piezo Speaker
  LED1 = LED - 3mm [color="Green (570nm)" current=0.030A package="3 mm [THT]"]
  LED2 = LED - 3mm [color="Red (633nm)" current=0.030A package="3 mm [THT]"]
  LED3 = LED - 3mm [color="Yellow (595nm)" current=0.030A package="3 mm [THT]"]
  U3 = Voltage Regulator - 5V [package="DPak [SMD]"]
  VCC1 = Battery block 9V [internal_resistance=0.1Ω]
  S1 = Pushbutton [package=THT]
  R1 = Resistor [tolerance=±5% resistance=1k package="0402 [SMD]"]  # not connected
  C1 = Tantalum Capacitor [capacitance=0.22µF voltage=35V package="A 3216 [SMD, tantalum]"]

nets:
  N1: µC1.PB0, U1.DB0
  N2: µC1.PB1, U1.DB1
  N3: µC1.PB2, U1.DB2
  N4: µC1.PB3, U1.DB3
  N5: µC1.PB4, U1.DB4
  N6: µC1.PB5, U1.DB5
  N7: µC1.PB6, U1.DB6
  N8: µC1.PB7, U1.DB7
  N9: µC1.RESET, S1.leg0, C1.+
  VCC: µC1.VCC, U1.VDD, U1.A, U2.G$1_E, U3.output_voltage
  GND1: µC1.GND1, µC1.GND2, U1.VSS, U1.K, U2.G$1_A, J1.pin1, LED1.anode, U3.GND, VCC1.-, S1.leg1, C1.-
  N10: µC1.PD0, U1.RS
  N11: µC1.PD1, U1.R_W
  N12: µC1.PD2, U1.E
  N13: µC1.PD3, LED1.cathode
  N14: µC1.PD4, LED3.cathode
  N15: µC1.PD5, LED2.cathode
  N16: µC1.PD6, J1.pin2
  N17: µC1.PC0, Matrix_keypad1.row1
  N18: µC1.PC1, Matrix_keypad1.row2
  N19: µC1.PC2, Matrix_keypad1.row3
  N20: µC1.PC3, Matrix_keypad1.row4
  N21: µC1.PC4, Matrix_keypad1.col1
  N22: µC1.PC5, Matrix_keypad1.col2
  N23: µC1.PC6, Matrix_keypad1.col3
  N24: µC1.PC7, Matrix_keypad1.col4
  N25: U1.VO, U2.G$2_1
  N26: U3.input_voltage, VCC1.+

custom parts:
  ATmega32: AVR 8-bit microcontroller.
  KEYPAD 4x4: Matrix keypad 16 buttons, 4 rows x 4 columns
